// Logisim project L11.circ as structural Verilog: 1 circuit, main circuit main
module main (
  input  D0,
  input  D1,
  input  D2,
  input  D3,
  input  D4,
  input  D5,
  input  D6,
  input  E,
  input  D7,
  input  [2:0] in_10
);

  wire multiplexer_1_out;

  Multiplexer #(.select(3)) multiplexer_1 (
    .in0(D0), .in1(D1), .in2(D2), .in3(D3), .in4(D4), .in5(D5), .in6(D6), .in7(D7), .out(multiplexer_1_out),
    .sel(in_10), .en(E));
  LED led_1 (.in(multiplexer_1_out));

  // Notes on the sheet:
  //   8X1 MUX 
endmodule
