// Logisim project L12.circ as structural Verilog: 1 circuit, main circuit main
module main (
  input  D0,
  input  D1,
  input  D2,
  input  D3,
  input  D4,
  input  D5,
  input  S2,
  input  D6,
  input  D7,
  input  S1,
  input  S0
);

  wire multiplexer_1_out, multiplexer_2_out, multiplexer_3_out, multiplexer_4_out, multiplexer_5_out,
       multiplexer_6_out, multiplexer_7_out;

  Multiplexer multiplexer_1 (.in0(D0), .in1(D1), .out(multiplexer_1_out), .sel(S0));  // open: en
  Multiplexer multiplexer_2 (.in0(D2), .in1(D3), .out(multiplexer_2_out), .sel(S0));  // open: en
  Multiplexer multiplexer_3 (.in0(D4), .in1(D5), .out(multiplexer_3_out), .sel(S0));  // open: en
  Multiplexer multiplexer_4 (.in0(D6), .in1(D7), .out(multiplexer_4_out), .sel(S0));  // open: en
  Multiplexer multiplexer_5 (
    .in0(multiplexer_1_out), .in1(multiplexer_2_out), .out(multiplexer_5_out), .sel(S1));  // open: en
  Multiplexer multiplexer_6 (
    .in0(multiplexer_3_out), .in1(multiplexer_4_out), .out(multiplexer_6_out), .sel(S1));  // open: en
  Multiplexer multiplexer_7 (
    .in0(multiplexer_5_out), .in1(multiplexer_6_out), .out(multiplexer_7_out), .sel(S2));  // open: en
  LED led_1 (.in(multiplexer_7_out));

  // Notes on the sheet:
  //   8X1 MUX USING 2X1 MUX
endmodule
