// Logisim project L13.circ as structural Verilog: 1 circuit, main circuit main
module main (
  input  I0,
  input  I1,
  input  I2,
  input  I3,
  input  I4,
  input  I5,
  input  in_7,
  input  I6,
  input  I7,
  input  I5_2,
  input  I4_2,
  input  I0_2,
  input  I1_2,
  input  I2_2,
  input  I3_2,
  input  I7_2,
  input  I6_2,
  output [2:0] out_18,
  output out_19,
  output out_20,
  output out_21
);

  or Y0 (out_21, I1_2, I3_2, I7_2, I5_2);
  or Y1 (out_19, I2_2, I3_2, I6_2, I7_2);
  Priority_Encoder priority_encoder_1 (
    .in0(I0), .in1(I1), .in2(I2), .in3(I3), .in4(I4), .in5(I5), .in6(I6), .in7(I7), .out(out_18), .en_in(in_7));  // open: gs, en_out
  or Y2 (out_20, I7_2, I6_2, I5_2, I4_2);

  // Notes on the sheet:
  //   8X3 ENCODER USING PRIORITY ENCODER AND OR GATES
endmodule
