// Logisim project L21.circ as structural Verilog: 1 circuit, main circuit main
module main (
  input  A0,
  input  B0,
  input  C_in,
  input  A1,
  input  B1,
  input  A2,
  input  B2,
  input  A3,
  input  B3,
  output S0,
  output C0,
  output S1,
  output C1,
  output S2,
  output C2,
  output S3,
  output C3
);

  wire and_1_out, and_2_out, and_3_out, and_4_out, and_5_out, and_6_out, and_7_out, and_8_out, and_9_out,
       and_10_out, and_11_out, and_12_out, and_13_out, and_14_out, and_15_out, and_16_out, and_17_out,
       and_18_out, and_19_out, and_20_out, and_21_out, and_22_out, and_23_out, and_24_out, not_1_out,
       not_2_out, not_3_out, not_4_out, not_5_out, not_6_out, not_7_out, not_8_out, not_9_out, not_10_out,
       not_11_out, not_12_out, not_13_out, not_14_out, not_15_out, not_16_out, or_1_out, or_2_out, or_3_out,
       or_4_out;

  not not_1 (not_1_out, A0);
  not not_2 (not_2_out, B0);
  not not_3 (not_3_out, A1);
  not not_4 (not_4_out, B1);
  not not_5 (not_5_out, A2);
  not not_6 (not_6_out, B2);
  not not_7 (not_7_out, A3);
  not not_8 (not_8_out, B3);
  and and_1 (and_1_out, A0, not_2_out);
  and and_2 (and_2_out, not_1_out, B0);
  and and_3 (and_3_out, A0, B0);
  and and_4 (and_4_out, A1, not_4_out);
  and and_5 (and_5_out, not_3_out, B1);
  and and_6 (and_6_out, A1, B1);
  and and_7 (and_7_out, A2, not_6_out);
  and and_8 (and_8_out, not_5_out, B2);
  and and_9 (and_9_out, A2, B2);
  and and_10 (and_10_out, A3, not_8_out);
  and and_11 (and_11_out, not_7_out, B3);
  and and_12 (and_12_out, A3, B3);
  or or_1 (or_1_out, and_1_out, and_2_out);
  or or_2 (or_2_out, and_4_out, and_5_out);
  or or_3 (or_3_out, and_7_out, and_8_out);
  or or_4 (or_4_out, and_10_out, and_11_out);
  not not_9 (not_9_out, or_1_out);
  not not_10 (not_10_out, C_in);
  not not_11 (not_11_out, or_2_out);
  not not_12 (not_12_out, C0);
  not not_13 (not_13_out, or_3_out);
  not not_14 (not_14_out, C1);
  not not_15 (not_15_out, or_4_out);
  not not_16 (not_16_out, C2);
  and and_13 (and_13_out, or_1_out, not_10_out);
  and and_14 (and_14_out, not_9_out, C_in);
  and and_15 (and_15_out, C_in, or_1_out);
  and and_16 (and_16_out, or_2_out, not_12_out);
  and and_17 (and_17_out, not_11_out, C0);
  and and_18 (and_18_out, C0, or_2_out);
  and and_19 (and_19_out, or_3_out, not_14_out);
  and and_20 (and_20_out, not_13_out, C1);
  and and_21 (and_21_out, C1, or_3_out);
  and and_22 (and_22_out, or_4_out, not_16_out);
  and and_23 (and_23_out, not_15_out, C2);
  and and_24 (and_24_out, C2, or_4_out);
  or or_5 (S0, and_13_out, and_14_out);
  or or_6 (S1, and_16_out, and_17_out);
  or or_7 (S2, and_19_out, and_20_out);
  Clock clock_1 (.out(S0));
  // Probe on S1
  Clock clock_2 (.out(S1));
  Clock clock_3 (.out(S2));
  or or_8 (S3, and_22_out, and_23_out);
  or or_9 (C0, and_15_out, and_3_out);
  or or_10 (C1, and_18_out, and_6_out);
  // Probe on S2
  or or_11 (C2, and_21_out, and_9_out);
  // Probe on S3
  Clock clock_4 (.out(S3));
  or or_12 (C3, and_24_out, and_12_out);

  // Notes on the sheet:
  //   C0
  //   C1
  //   C2
endmodule
